// Logisim project ALU.circ as structural Verilog: 1 circuit, main circuit main
module main (
  input  Cin,
  input  [15:0] B,
  input  [15:0] C,
  input  [3:0] op,
  output [15:0] ACC,
  output ZERO,
  output NEGATIVE,
  output OVERFLOW
);

  wire adder_1_cout, comparator_1_eq, not_2_out, or_2_out, or_3_out;
  wire [15:0] adder_1_out, and_1_out, divider_1_out, multiplier_1_cout, multiplier_1_out, not_1_out,
       or_1_out, shifter_1_out, shifter_2_out, subtractor_1_out, xor_1_out;

  assign not_1_out = ~B;  // NOT_Gate not_1, 16 bits wide
  assign and_1_out = B & C;  // AND_Gate and_1, 16 bits wide
  assign or_1_out = B | C;  // OR_Gate or_1, 16 bits wide
  Adder #(.width(16)) adder_1 (.a(B), .b(C), .out(adder_1_out), .cin(Cin), .cout(adder_1_cout));
  Subtractor #(.width(16)) subtractor_1 (.a(B), .b(C), .out(subtractor_1_out));  // open: bin, bout
  Multiplier #(.width(16)) multiplier_1 (
    .a(B), .b(C), .out(multiplier_1_out), .cin({16{1'b0}}), .cout(multiplier_1_cout));
  Divider #(.width(16)) divider_1 (.a(B), .b(C), .out(divider_1_out), .upper({16{1'b0}}));  // open: rem
  assign xor_1_out = B ^ C;  // XOR_Gate xor_1, 16 bits wide
  Shifter #(.width(16)) shifter_1 (.in(B), .\dist (C[3:0]), .out(shifter_1_out));
  Shifter #(.shift("lr"), .width(16)) shifter_2 (.in(B), .\dist (C[3:0]), .out(shifter_2_out));
  Comparator #(.width(16)) comparator_1 (.a(B), .b(C), .eq(comparator_1_eq), .lt(NEGATIVE));  // open: gt
  Multiplexer #(.select(4), .width(16)) multiplexer_1 (
    .in0(adder_1_out), .in1(subtractor_1_out), .in2(multiplier_1_out), .in3(divider_1_out), .in4(not_1_out),
    .in5(and_1_out), .in6(or_1_out), .in7(shifter_1_out), .in8(shifter_2_out), .in9(xor_1_out), .out(ACC),
    .sel(op));  // open: in10, in11, in12, in13, in14, in15
  or or_2 (or_2_out, multiplier_1_cout[0], multiplier_1_cout[1], multiplier_1_cout[2], multiplier_1_cout[3], multiplier_1_cout[4], multiplier_1_cout[5], multiplier_1_cout[6], multiplier_1_cout[7], multiplier_1_cout[8], multiplier_1_cout[9], multiplier_1_cout[10], multiplier_1_cout[11], multiplier_1_cout[12], multiplier_1_cout[13], multiplier_1_cout[14], multiplier_1_cout[15]);
  or or_3 (or_3_out, ACC[0], ACC[1], ACC[2], ACC[3], ACC[4], ACC[5], ACC[6], ACC[7], ACC[8], ACC[9], ACC[10], ACC[11], ACC[12], ACC[13], ACC[14], ACC[15]);
  not not_2 (not_2_out, or_3_out);
  or or_4 (ZERO, not_2_out, comparator_1_eq);
  or or_5 (OVERFLOW, adder_1_cout, or_2_out);
endmodule
