// Logisim project RegisterBankCirc.circ as structural Verilog: 2 circuits, main circuit main
module RegisterBank (
  input  [15:0] A,
  input  [15:0] B,
  input  [15:0] C,
  input  [15:0] ACCIN,
  input  [15:0] IR,
  input  [15:0] PC,
  input  [15:0] LR,
  input  CLK,
  input  [6:0] RegisterClearSelect,
  input  [6:0] RegisterEnableSelect,
  output [15:0] ACCOUT
);

  wire [15:0] InstructionRegister_q;

  Register #(.width(16)) LinkRegister (
    .D(LR), .en(RegisterEnableSelect[0]), .clk(CLK), .Q(LR), .clr(RegisterClearSelect[6]));
  Register #(.width(16)) RegisterA (
    .D(A), .en(RegisterEnableSelect[6]), .clk(CLK), .Q(A), .clr(RegisterClearSelect[4]));
  Register #(.width(16)) RegisterB (
    .D(B), .en(RegisterEnableSelect[5]), .clk(CLK), .Q(B), .clr(RegisterClearSelect[3]));
  Register #(.width(16)) RegisterC (
    .D(C), .en(RegisterEnableSelect[4]), .clk(CLK), .Q(C), .clr(RegisterClearSelect[2]));
  Register #(.width(16)) accumulator (
    .D(ACCIN), .en(RegisterEnableSelect[3]), .clk(CLK), .Q(ACCOUT), .clr(RegisterClearSelect[1]));
  Register #(.width(16)) InstructionRegister (
    .D(IR), .en(RegisterEnableSelect[2]), .clk(CLK), .Q(InstructionRegister_q), .clr(RegisterClearSelect[0]));
  Register #(.width(16)) ProgramCounter (
    .D(PC), .en(RegisterEnableSelect[1]), .clk(CLK), .Q(PC), .clr(RegisterClearSelect[5]));
endmodule

module main (
);

  RegisterBank registerbank_1 ();  // open: A, B, C, ACCIN, IR, PC, LR, CLK, RegisterClearSelect, RegisterEnableSelect, ACCOUT
endmodule
