// Logisim project brachocpu.circ as structural Verilog
module cpu (
  input  DataDebugEnable,
  input  AddressDebugEnable,
  input  ControlDebugEnable,
  input  [11:0] AddressBus,
  input  [15:0] DataBus,
  input  Reset,
  input  UnHALT,
  output AO,
  output BO,
  output CO,
  output ACO,
  output IOD,
  output PO,
  output LO,
  output IOA,
  output AI,
  output BI,
  output CI,
  output II,
  output PI,
  output LI,
  output PID,
  output INC,
  output Print,
  output CinALU,
  output RI,
  output RO
);

  wire controlled_buffer_4_out, MAINCLOCK_out, not_1_out, or_1_out, pull_resistor_5_node, rgb_video_1_p3;
  wire [2:0] alu_1_zero, flagsregister_1_flagsout;
  wire [7:0] registerbank_1_irout;
  wire [11:0] controlled_buffer_1_out;
  wire [15:0] AC, alu_1_acc, AR, BR, controlled_buffer_3_out, CR, LR, PC, ram_1_dout, registerbank_1_dataout,
       RI_t;
  wire [16:0] pull_resistor_2_node;
  wire [19:17] pull_resistor_2_node_2;

  assign controlled_buffer_1_out = AddressDebugEnable ? AddressBus : 12'bz;  // Controlled_Buffer controlled_buffer_1
  assign {RO, RI, CinALU, Print, INC, PID, LI, PI, II, CI, BI, AI, IOA, LO, PO, IOD, ACO, CO, BO, AO} = ControlDebugEnable ? {pull_resistor_2_node_2, pull_resistor_2_node} : 20'bz;  // Controlled_Buffer controlled_buffer_2
  or or_1 (or_1_out, UnHALT, not_1_out);
  assign controlled_buffer_3_out = DataDebugEnable ? DataBus : 16'bz;  // Controlled_Buffer controlled_buffer_3
  assign controlled_buffer_4_out = or_1_out ? MAINCLOCK_out : 1'bz;  // Controlled_Buffer controlled_buffer_4
  Pull_Resistor pull_resistor_1 (.node(or_1_out));
  Pull_Resistor pull_resistor_2 (.node({pull_resistor_2_node_2, pull_resistor_2_node}));
  Pull_Resistor pull_resistor_3 (.node(controlled_buffer_3_out));
  not not_1 (not_1_out, pull_resistor_5_node);
  Pull_Resistor pull_resistor_4 (.node(controlled_buffer_1_out));
  Pull_Resistor pull_resistor_5 (.node(pull_resistor_5_node));
  Hex_Digit_Display hex_digit_display_1 (.value(AC[15:12]));  // open: dp
  Hex_Digit_Display hex_digit_display_2 (.value(AC[11:8]));  // open: dp
  Hex_Digit_Display hex_digit_display_3 (.value(AC[7:4]));  // open: dp
  Hex_Digit_Display hex_digit_display_4 (.value(AC[3:0]));  // open: dp
  ALU alu_1 (
    .Cin(pull_resistor_2_node_2[17]), .B(BR), .C(CR), .op(registerbank_1_irout[3:0]), .IRout(RI_t),
    .ACC(alu_1_acc), .ZERO(alu_1_zero[0]), .NEGATIVE(alu_1_zero[1]), .OVERFLOW(alu_1_zero[2]));
  FlagsRegister flagsregister_1 (
    .Flags(alu_1_zero), .Opcodes(registerbank_1_irout), .CLK(controlled_buffer_4_out), .Clear(Reset),
    .FlagsOut(flagsregister_1_flagsout));
  RegisterBank registerbank_1 (
    .Clear(Reset), .CLK(controlled_buffer_4_out), .ACC(alu_1_acc), .COUT(rgb_video_1_p3),
    .AddressBusIN(controlled_buffer_1_out), .ControlBus(pull_resistor_2_node),
    .DataBusIN(controlled_buffer_3_out), .AddressBusOUT(controlled_buffer_1_out),
    .DataBusOUT(controlled_buffer_3_out), .DataOUT(registerbank_1_dataout), .Aout(AR), .BALU(BR), .CALU(CR),
    .ACCout(AC), .IRout(registerbank_1_irout), .RIoutFull(RI_t), .PCout(PC), .LRout(LR));
  Pull_Resistor pull_resistor_6 (.node(registerbank_1_dataout));
  Hex_Digit_Display hex_digit_display_5 (.value(RI_t[15:12]));  // open: dp
  Hex_Digit_Display hex_digit_display_6 (.value(RI_t[11:8]));  // open: dp
  Hex_Digit_Display hex_digit_display_7 (.value(RI_t[7:4]));  // open: dp
  // RGB_Video #(.height(64), .scale(4), .width(64)) rgb_video_1: pin names not known; wires that end beside it: Reset, controlled_buffer_4_out, rgb_video_1_p3, registerbank_1_dataout[15:10], registerbank_1_dataout[9:4], registerbank_1_dataout[3:0]
  Hex_Digit_Display hex_digit_display_8 (.value(RI_t[3:0]));  // open: dp
  ControlUnit controlunit_1 (
    .Flag(flagsregister_1_flagsout), .IRout(registerbank_1_irout), .Clear(Reset),
    .CLK(controlled_buffer_4_out), .COUT(rgb_video_1_p3), .HALT(pull_resistor_5_node),
    .ControlBus({pull_resistor_2_node_2, pull_resistor_2_node}));
  // Probe on registerbank_1_dataout
  Hex_Digit_Display hex_digit_display_9 (.value(LR[15:12]));  // open: dp
  // Probe on controlled_buffer_3_out
  Hex_Digit_Display hex_digit_display_10 (.value(LR[11:8]));  // open: dp
  Hex_Digit_Display hex_digit_display_11 (.value(LR[7:4]));  // open: dp
  assign controlled_buffer_3_out = pull_resistor_2_node_2[19] ? ram_1_dout : 16'bz;  // Controlled_Buffer controlled_buffer_5
  Hex_Digit_Display hex_digit_display_12 (.value(LR[3:0]));  // open: dp
  RAM #(.addrWidth(12), .dataWidth(16), .trigger("high"), .\type ("nonvolatile")) ram_1 (
    .addr(controlled_buffer_1_out), .we(pull_resistor_2_node_2[18]), .oe(1'b1),
    .din(controlled_buffer_3_out), .dout(ram_1_dout));
  Hex_Digit_Display hex_digit_display_13 (.value(PC[15:12]));  // open: dp
  Hex_Digit_Display hex_digit_display_14 (.value(PC[11:8]));  // open: dp
  Hex_Digit_Display hex_digit_display_15 (.value(PC[7:4]));  // open: dp
  Hex_Digit_Display hex_digit_display_16 (.value(PC[3:0]));  // open: dp
  Clock MAINCLOCK (.out(MAINCLOCK_out));
  Hex_Digit_Display hex_digit_display_17 (.value(AR[15:12]));  // open: dp
  Hex_Digit_Display hex_digit_display_18 (.value(BR[15:12]));  // open: dp
  Hex_Digit_Display hex_digit_display_19 (.value(CR[15:12]));  // open: dp
  // Probe on AR
  Hex_Digit_Display hex_digit_display_20 (.value(AR[11:8]));  // open: dp
  Hex_Digit_Display hex_digit_display_21 (.value(AR[7:4]));  // open: dp
  Hex_Digit_Display hex_digit_display_22 (.value(BR[11:8]));  // open: dp
  Hex_Digit_Display hex_digit_display_23 (.value(BR[7:4]));  // open: dp
  Hex_Digit_Display hex_digit_display_24 (.value(CR[11:8]));  // open: dp
  Hex_Digit_Display hex_digit_display_25 (.value(CR[7:4]));  // open: dp
  Hex_Digit_Display hex_digit_display_26 (.value(AR[3:0]));  // open: dp
  Hex_Digit_Display hex_digit_display_27 (.value(BR[3:0]));  // open: dp
  Hex_Digit_Display hex_digit_display_28 (.value(CR[3:0]));  // open: dp

  // Notes on the sheet:
  //   Accumulator
  //   Instruction Register
  //   Crontrol Bus
  //   Link Register
  //   Program Counter
  //   RAM
  //   A Register
  //   B Register
  //   C Register
endmodule

module ALU (
  input  Cin,
  input  [15:0] B,
  input  [15:0] C,
  input  [3:0] op,
  input  [15:0] IRout,
  output [15:0] ACC,
  output ZERO,
  output NEGATIVE,
  output OVERFLOW
);

  wire adder_1_cout, sixteeninputor_1_out_2, sixteeninputor_2_out_2;
  wire [15:0] adder_1_out, and_1_out, divider_1_out, multiplier_1_cout, multiplier_1_out, nor_1_out,
       not_1_out, or_1_out, shifter_1_out, shifter_2_out, subtractor_1_out, xor_1_out;

  assign not_1_out = ~B;  // NOT_Gate not_1, 16 bits wide
  assign and_1_out = B & C;  // AND_Gate and_1, 16 bits wide
  assign or_1_out = B | C;  // OR_Gate or_1, 16 bits wide
  Adder #(.width(16)) adder_1 (.a(B), .b(C), .out(adder_1_out), .cin(Cin), .cout(adder_1_cout));
  Subtractor #(.width(16)) subtractor_1 (.a(B), .b(C), .out(subtractor_1_out));  // open: bin, bout
  Multiplier #(.width(16)) multiplier_1 (
    .a(B), .b(C), .out(multiplier_1_out), .cin({16{1'b0}}), .cout(multiplier_1_cout));
  Divider #(.width(16)) divider_1 (.a(B), .b(C), .out(divider_1_out), .upper({16{1'b0}}));  // open: rem
  assign xor_1_out = B ^ C;  // XOR_Gate xor_1, 16 bits wide
  Shifter #(.width(16)) shifter_1 (.in(B), .\dist (IRout[3:0]), .out(shifter_1_out));
  Shifter #(.shift("lr"), .width(16)) shifter_2 (.in(B), .\dist (IRout[3:0]), .out(shifter_2_out));
  Multiplexer #(.select(4), .width(16)) multiplexer_1 (
    .in0(adder_1_out), .in1(subtractor_1_out), .in2(multiplier_1_out), .in3(divider_1_out), .in4(not_1_out),
    .in5(and_1_out), .in6(or_1_out), .in7(shifter_1_out), .in8(shifter_2_out), .in9(xor_1_out),
    .in10({16{1'b0}}), .in11({16{1'b0}}), .in12({16{1'b0}}), .in13({16{1'b0}}), .in14({16{1'b0}}),
    .in15({16{1'b0}}), .out(ACC), .sel(op));
  assign nor_1_out = ~(C | B);  // NOR_Gate nor_1, 16 bits wide
  SixteenInputOR sixteeninputor_1 (.in_1(multiplier_1_cout), .out_2(sixteeninputor_1_out_2));
  SixteenInputOR sixteeninputor_2 (.in_1(ACC), .out_2(sixteeninputor_2_out_2));
  not not_2 (ZERO, sixteeninputor_2_out_2);
  SixteenInputAND sixteeninputand_1 (.in_1(nor_1_out), .out_2(NEGATIVE));
  or or_2 (OVERFLOW, adder_1_cout, sixteeninputor_1_out_2);
endmodule

module RegisterBank (
  input  [11:0] AddressBusIN,
  input  COUT,
  input  [15:0] DataBusIN,
  input  [16:0] ControlBus,
  input  [15:0] ACC,
  input  CLK,
  input  Clear,
  output [11:0] AddressBusOUT,
  output [15:0] DataBusOUT,
  output [15:0] DataOUT,
  output [15:0] Aout,
  output [15:0] BALU,
  output [15:0] CALU,
  output [15:0] ACCout,
  output [7:0] IRout,
  output [15:0] RIoutFull,
  output [15:0] PCout,
  output [15:0] LRout
);

  wire [6:0] pull_resistor_1_node;
  wire [11:0] LinkRegister_q, programcounter_1_addressbusout;
  wire [15:0] bit_extender_1_out;

  // Probe on DataBusIN
  // Probe on ControlBus[14]
  // Probe on ControlBus[15]
  // Probe on pull_resistor_1_node
  // Probe on ControlBus[13:8]
  Pull_Resistor pull_resistor_1 (.node(pull_resistor_1_node));
  assign pull_resistor_1_node = Clear ? {7{1'b1}} : 7'bz;  // Controlled_Buffer controlled_buffer_1
  // Probe on ControlBus[16]
  Register #(.width(12)) LinkRegister (
    .D(DataBusIN[11:0]), .en(ControlBus[13]), .clk(CLK), .Q(LinkRegister_q), .clr(pull_resistor_1_node[6]));
  Register #(.width(16)) RegisterA (
    .D(DataBusIN), .en(ControlBus[8]), .clk(CLK), .Q(Aout), .clr(pull_resistor_1_node[0]));
  Register #(.width(16)) RegisterB (
    .D(DataBusIN), .en(ControlBus[9]), .clk(CLK), .Q(BALU), .clr(pull_resistor_1_node[1]));
  Register #(.width(16)) RegisterC (
    .D(DataBusIN), .en(ControlBus[10]), .clk(CLK), .Q(CALU), .clr(pull_resistor_1_node[2]));
  Register #(.width(16)) accumulator (.D(ACC), .en(1'b1), .clk(CLK), .Q(ACCout), .clr(pull_resistor_1_node[3]));
  Register #(.width(16)) InstructionRegister (
    .D(DataBusIN), .en(ControlBus[11]), .clk(CLK), .Q({IRout, RIoutFull[7:0]}), .clr(pull_resistor_1_node[4]));
  Pull_Resistor pull_resistor_2 (.node(ControlBus));
  assign DataBusOUT = ControlBus[1] ? BALU : 16'bz;  // Controlled_Buffer controlled_buffer_2
  assign DataBusOUT = ControlBus[2] ? CALU : 16'bz;  // Controlled_Buffer controlled_buffer_3
  assign DataBusOUT = ControlBus[3] ? ACCout : 16'bz;  // Controlled_Buffer controlled_buffer_4
  assign DataBusOUT = ControlBus[4] ? bit_extender_1_out : 16'bz;  // Controlled_Buffer controlled_buffer_5
  assign bit_extender_1_out = {{4{1'b0}}, {IRout[3:0], RIoutFull[7:0]}};  // Bit_Extender bit_extender_1
  // Probe on ControlBus[7:0]
  assign DataBusOUT = ControlBus[0] ? Aout : 16'bz;  // Controlled_Buffer controlled_buffer_6
  Programcounter programcounter_1 (
    .DataBus(DataBusIN), .AdressBus(AddressBusIN), .PIDATA(ControlBus[14]), .INC(ControlBus[15]),
    .PI(ControlBus[12]), .CLK(CLK), .R(pull_resistor_1_node[5]),
    .AddressBusOUT(programcounter_1_addressbusout));
  assign AddressBusOUT = ControlBus[6] ? LinkRegister_q : 12'bz;  // Controlled_Buffer controlled_buffer_7
  assign AddressBusOUT = ControlBus[7] ? {IRout[3:0], RIoutFull[7:0]} : 12'bz;  // Controlled_Buffer controlled_buffer_8
  assign AddressBusOUT = ControlBus[5] ? programcounter_1_addressbusout : 12'bz;  // Controlled_Buffer controlled_buffer_9
  assign DataOUT = COUT ? Aout : 16'bz;  // Controlled_Buffer controlled_buffer_10
  assign PCout = {{4{1'b0}}, programcounter_1_addressbusout};  // Bit_Extender bit_extender_2
  assign LRout = {{4{1'b0}}, LinkRegister_q};  // Bit_Extender bit_extender_3

  assign RIoutFull[15:8] = IRout;

  // Notes on the sheet:
  //   DataOUT: pull=down
  //   Aout: pull=down
endmodule

module Programcounter (
  input  [15:0] DataBus,
  input  [11:0] AdressBus,
  input  PIDATA,
  input  INC,
  input  PI,
  input  CLK,
  input  R,
  output [11:0] AddressBusOUT
);

  wire counter_1_carry, not_1_out, or_1_out;
  wire [15:0] controlled_buffer_1_out;

  or or_1 (or_1_out, counter_1_carry, R);
  assign controlled_buffer_1_out = PIDATA ? DataBus : 16'bz;  // Controlled_Buffer controlled_buffer_1
  assign controlled_buffer_1_out[11:0] = not_1_out ? AdressBus : 12'bz;  // Controlled_Buffer controlled_buffer_2
  not not_1 (not_1_out, PIDATA);
  Counter #(.max('hfff), .width(12)) counter_1 (
    .clr(or_1_out), .load(PI), .up(1'b1), .count(INC), .clk(CLK), .D(controlled_buffer_1_out[11:0]),
    .carry(counter_1_carry), .Q(AddressBusOUT));
endmodule

module SixteenInputOR (
  input  [15:0] in_1,
  output out_2
);

  or or_1 (out_2, in_1[0], in_1[1], in_1[2], in_1[3], in_1[4], in_1[5], in_1[6], in_1[7], in_1[8], in_1[9], in_1[10], in_1[11], in_1[12], in_1[13], in_1[14], in_1[15]);
endmodule

module ControlUnit (
  input  [2:0] Flag,
  input  [7:0] IRout,
  input  Clear,
  input  CLK,
  output COUT,
  output HALT,
  output [19:0] ControlBus
);

  wire and_1_out, and_2_out, and_3_out, and_4_out, and_5_out, and_6_out, and_7_out, and_8_out, BR,
       nand_1_out, not_1_out, not_2_out, not_3_out, not_4_out, not_5_out, not_6_out, not_7_out, not_8_out,
       not_9_out, or_2_out;
  wire [1:0] counter_1_q;
  wire [4:0] BROUT, multiplexer_1_out, multiplexer_2_out;
  wire [19:0] rom_1_data;

  // Probe on Flag[2]
  // Probe on Flag[1]
  // Probe on Flag[0]
  not not_1 (not_1_out, CLK);
  not not_2 (not_2_out, IRout[7]);
  not not_3 (not_3_out, IRout[5]);
  not not_4 (not_4_out, IRout[6]);
  not not_5 (not_5_out, IRout[4]);
  not not_6 (not_6_out, IRout[5]);
  not not_7 (not_7_out, IRout[6]);
  Counter #(.max('h3), .width(2)) counter_1 (
    .clr(Clear), .load(1'b0), .up(1'b1), .count(1'b1), .clk(not_1_out), .D(2'b00), .Q(counter_1_q));  // open: carry
  and and_1 (and_1_out, IRout[4], not_3_out, not_4_out, IRout[7]);
  and and_2 (and_2_out, not_5_out, not_6_out, not_7_out, IRout[7]);
  and and_3 (and_3_out, IRout[4], IRout[5], IRout[6], not_2_out);
  // Probe on and_2_out
  // Probe on and_3_out
  // Probe on and_1_out
  Multiplexer #(.width(5)) multiplexer_1 (
    .in0({4'b0000, counter_1_q[0]}), .in1({1'b1, IRout[7:4]}), .out(multiplexer_1_out), .sel(counter_1_q[1]));
  Multiplexer #(.width(5)) multiplexer_2 (
    .in0(BROUT), .in1(multiplexer_1_out), .out(multiplexer_2_out), .sel(nand_1_out));
  nand nand_1 (nand_1_out, BR, not_8_out, counter_1_q[1]);
  and and_4 (and_4_out, and_2_out, Flag[0]);
  and and_5 (and_5_out, and_3_out, Flag[1]);
  and and_6 (and_6_out, and_1_out, Flag[2]);
  // Probe on multiplexer_2_out
  not not_8 (not_8_out, counter_1_q[0]);
  or or_1 (BR, and_2_out, and_3_out, and_1_out);
  and and_7 (and_7_out, IRout[4], IRout[6], IRout[7]);
  ROM #(.addrWidth(5), .dataWidth(20)) rom_1 (.addr(multiplexer_2_out), .data(rom_1_data));
  and and_8 (and_8_out, counter_1_q[1], counter_1_q[0]);
  or or_2 (or_2_out, and_4_out, and_5_out, and_6_out);
  not not_9 (not_9_out, IRout[5]);
  and and_9 (COUT, not_9_out, and_7_out);
  and and_10 (HALT, IRout[5], and_7_out);
  Multiplexer #(.width(20)) multiplexer_3 (.in0(rom_1_data), .in1({20{1'b0}}), .out(ControlBus), .sel(and_8_out));
  Multiplexer #(.width(5)) multiplexer_4 (.in0(5'b11110), .in1(5'b10110), .out(BROUT), .sel(or_2_out));

  // Other names for the same wires on the sheet: Code[3:0] = IRout[7:4]; Flags[2:0] = Flag

  // Notes on the sheet:
  //   ControlBus: pull=up
  //   Clear: pull=down
  //   contents of rom_1 (hex, n*v repeats v):
  //   80820 8000 15*0 210 410 80280 80480 40081 1080 0 0 0 82080 80140 0 0 108
  //   Crontrol Unit Logic
  //   BR instruction
  //   NOP instruction
endmodule

module ControlBusSchema (
  output AO,
  output BO,
  output CO,
  output ACO,
  output IOD,
  output PO,
  output LO,
  output IOA,
  output AI,
  output BI,
  output CI,
  output II,
  output PI,
  output LI,
  output PID,
  output INC,
  output RESET,
  output CinALU,
  output RI,
  output RO
);

  // Probe on {RO, RI, CinALU, RESET, INC, PID, LI, PI, II, CI, BI, AI, IOA, LO, PO, IOD, ACO, CO, BO, AO}
endmodule

module FlagsRegister (
  input  [2:0] Flags,
  input  [7:0] Opcodes,
  input  CLK,
  input  Clear,
  output [2:0] FlagsOut
);

  wire nor_1_out;

  nor nor_1 (nor_1_out, Opcodes[0], Opcodes[1], Opcodes[2], Opcodes[3]);
  Register #(.width(3)) register_1 (.D(Flags), .en(nor_1_out), .clk(CLK), .Q(FlagsOut), .clr(Clear));
endmodule

module SixteenInputAND (
  input  [15:0] in_1,
  output out_2
);

  and and_1 (out_2, in_1[0], in_1[1], in_1[2], in_1[3], in_1[4], in_1[5], in_1[6], in_1[7], in_1[9], in_1[10], in_1[11], in_1[12], in_1[13], in_1[14], in_1[15], in_1[8]);
endmodule
